// Logisim project Program_Counter.circ as structural Verilog: 9 circuits, main circuit main
module main (
  input  in_1,
  input  [7:0] in_2,
  input  in_3,
  input  in_4,
  input  in_5,
  input  in_6,
  input  [7:0] in_7,
  input  in_8,
  input  [7:0] in_9,
  input  in_10,
  input  in_11,
  input  in_12,
  input  in_13,
  input  in_14,
  input  in_15,
  input  in_16,
  output [7:0] out_17,
  output out_18,
  output [7:0] out_19,
  output [7:0] out_20,
  output [3:0] out_21
);

  wire [7:0] fariaz_reg_1_reg_int_out, fariaz_reg_2_reg_int_out;

  fariaz_reg fariaz_reg_1 (
    .reg_in(in_2), .reg_in_en(in_4), .reg_clk(in_5), .reg_out_en(in_6), .reg_int_out(fariaz_reg_1_reg_int_out));  // open: reg_out
  fariaz_reg fariaz_reg_2 (
    .reg_in(in_7), .reg_in_en(in_8), .reg_clk(in_5), .reg_int_out(fariaz_reg_2_reg_int_out));  // open: reg_out_en, reg_out
  fariaz_pc fariaz_pc_1 (.pc_en(in_13), .pc_clk(in_14), .pc_reset(in_15), .pc_out_en(in_16), .pc_out(out_21));
  fariaz_reg fariaz_reg_3 (
    .reg_in(in_9), .reg_in_en(in_10), .reg_clk(in_11), .reg_out_en(in_12), .reg_int_out(out_19),
    .reg_out(out_20));
  fariaz_alu fariaz_alu_1 (
    .alu_in_1(fariaz_reg_1_reg_int_out), .alu_out_in(in_1), .alu_sub(in_3),
    .alu_in_2(fariaz_reg_2_reg_int_out), .alu_out(out_17), .alu_carry_out(out_18));
endmodule

module fariaz_reg (
  input  [7:0] reg_in,
  input  reg_in_en,
  input  reg_clk,
  input  reg_out_en,
  output [7:0] reg_int_out,
  output [7:0] reg_out
);

  wire multiplexer_1_out, multiplexer_2_out, multiplexer_3_out, multiplexer_4_out, multiplexer_5_out,
       multiplexer_6_out, multiplexer_7_out, multiplexer_8_out;

  Multiplexer multiplexer_1 (.in0(reg_int_out[7]), .in1(reg_in[7]), .out(multiplexer_1_out), .sel(reg_in_en));
  D_Flip_Flop d_ff_1 (.D(multiplexer_1_out), .clk(reg_clk), .Q(reg_int_out[7]));  // open: Qn, preset, reset
  Multiplexer multiplexer_2 (.in0(reg_int_out[6]), .in1(reg_in[6]), .out(multiplexer_2_out), .sel(reg_in_en));
  assign reg_out[7] = reg_out_en ? reg_int_out[7] : 1'bz;  // Controlled_Buffer controlled_buffer_1
  D_Flip_Flop d_ff_2 (.D(multiplexer_2_out), .clk(reg_clk), .Q(reg_int_out[6]));  // open: Qn, preset, reset
  Multiplexer multiplexer_3 (.in0(reg_int_out[5]), .in1(reg_in[5]), .out(multiplexer_3_out), .sel(reg_in_en));
  assign reg_out[6] = reg_out_en ? reg_int_out[6] : 1'bz;  // Controlled_Buffer controlled_buffer_2
  D_Flip_Flop d_ff_3 (.D(multiplexer_3_out), .clk(reg_clk), .Q(reg_int_out[5]));  // open: Qn, preset, reset
  Multiplexer multiplexer_4 (.in0(reg_int_out[4]), .in1(reg_in[4]), .out(multiplexer_4_out), .sel(reg_in_en));
  assign reg_out[5] = reg_out_en ? reg_int_out[5] : 1'bz;  // Controlled_Buffer controlled_buffer_3
  D_Flip_Flop d_ff_4 (.D(multiplexer_4_out), .clk(reg_clk), .Q(reg_int_out[4]));  // open: Qn, preset, reset
  Multiplexer multiplexer_5 (.in0(reg_int_out[3]), .in1(reg_in[3]), .out(multiplexer_5_out), .sel(reg_in_en));
  D_Flip_Flop d_ff_5 (.D(multiplexer_5_out), .clk(reg_clk), .Q(reg_int_out[3]));  // open: Qn, preset, reset
  assign reg_out[4] = reg_out_en ? reg_int_out[4] : 1'bz;  // Controlled_Buffer controlled_buffer_4
  assign reg_out[3] = reg_out_en ? reg_int_out[3] : 1'bz;  // Controlled_Buffer controlled_buffer_5
  Multiplexer multiplexer_6 (.in0(reg_int_out[2]), .in1(reg_in[2]), .out(multiplexer_6_out), .sel(reg_in_en));
  D_Flip_Flop d_ff_6 (.D(multiplexer_6_out), .clk(reg_clk), .Q(reg_int_out[2]));  // open: Qn, preset, reset
  Multiplexer multiplexer_7 (.in0(reg_int_out[1]), .in1(reg_in[1]), .out(multiplexer_7_out), .sel(reg_in_en));
  D_Flip_Flop d_ff_7 (.D(multiplexer_7_out), .clk(reg_clk), .Q(reg_int_out[1]));  // open: Qn, preset, reset
  assign reg_out[2] = reg_out_en ? reg_int_out[2] : 1'bz;  // Controlled_Buffer controlled_buffer_6
  assign reg_out[1] = reg_out_en ? reg_int_out[1] : 1'bz;  // Controlled_Buffer controlled_buffer_7
  Multiplexer multiplexer_8 (.in0(reg_int_out[0]), .in1(reg_in[0]), .out(multiplexer_8_out), .sel(reg_in_en));
  D_Flip_Flop d_ff_8 (.D(multiplexer_8_out), .clk(reg_clk), .Q(reg_int_out[0]));  // open: Qn, preset, reset
  assign reg_out[0] = reg_out_en ? reg_int_out[0] : 1'bz;  // Controlled_Buffer controlled_buffer_8
endmodule

module fariaz_alu (
  input  [7:0] alu_in_1,
  input  alu_out_in,
  input  alu_sub,
  input  [7:0] alu_in_2,
  output [7:0] alu_out,
  output alu_carry_out
);

  wire adder_2_cout, adder_3_cout, adder_4_cout, adder_5_cout, adder_6_cout, adder_7_cout, adder_8_cout,
       xor_1_out, xor_2_out, xor_3_out, xor_4_out, xor_5_out, xor_6_out, xor_7_out, xor_8_out;
  wire [7:0] adder_8_out;

  Adder #(.width(1)) adder_1 (
    .a(alu_in_1[7]), .b(xor_1_out), .out(adder_8_out[7]), .cin(adder_2_cout), .cout(alu_carry_out));
  xor xor_1 (xor_1_out, alu_in_2[7], alu_sub);
  xor xor_2 (xor_2_out, alu_in_2[6], alu_sub);
  Adder #(.width(1)) adder_2 (
    .a(alu_in_1[6]), .b(xor_2_out), .out(adder_8_out[6]), .cin(adder_3_cout), .cout(adder_2_cout));
  xor xor_3 (xor_3_out, alu_in_2[5], alu_sub);
  Adder #(.width(1)) adder_3 (
    .a(alu_in_1[5]), .b(xor_3_out), .out(adder_8_out[5]), .cin(adder_4_cout), .cout(adder_3_cout));
  Adder #(.width(1)) adder_4 (
    .a(alu_in_1[4]), .b(xor_4_out), .out(adder_8_out[4]), .cin(adder_5_cout), .cout(adder_4_cout));
  xor xor_4 (xor_4_out, alu_in_2[4], alu_sub);
  Adder #(.width(1)) adder_5 (
    .a(alu_in_1[3]), .b(xor_5_out), .out(adder_8_out[3]), .cin(adder_6_cout), .cout(adder_5_cout));
  xor xor_5 (xor_5_out, alu_in_2[3], alu_sub);
  Adder #(.width(1)) adder_6 (
    .a(alu_in_1[2]), .b(xor_6_out), .out(adder_8_out[2]), .cin(adder_7_cout), .cout(adder_6_cout));
  xor xor_6 (xor_6_out, alu_in_2[2], alu_sub);
  xor xor_7 (xor_7_out, alu_in_2[1], alu_sub);
  Adder #(.width(1)) adder_7 (
    .a(alu_in_1[1]), .b(xor_7_out), .out(adder_8_out[1]), .cin(adder_8_cout), .cout(adder_7_cout));
  xor xor_8 (xor_8_out, alu_in_2[0], alu_sub);
  Adder #(.width(1)) adder_8 (.a(alu_in_1[0]), .b(xor_8_out), .out(adder_8_out[0]), .cin(alu_sub), .cout(adder_8_cout));
  assign alu_out = alu_out_in ? adder_8_out : 8'bz;  // Controlled_Buffer controlled_buffer_1
endmodule

module fariaz_pc (
  input  pc_en,
  input  pc_clk,
  input  pc_reset,
  input  pc_out_en,
  output [3:0] pc_out
);

  wire j_k_ff_2_qn, j_k_ff_3_qn, j_k_ff_4_qn;
  wire [3:0] j_k_ff_4_q;

  J_K_Flip_Flop j_k_ff_1 (
    .J(pc_en), .K(pc_en), .clk(j_k_ff_2_qn), .Q(j_k_ff_4_q[3]), .reset(pc_reset));  // open: Qn, preset
  J_K_Flip_Flop j_k_ff_2 (
    .J(pc_en), .K(pc_en), .clk(j_k_ff_3_qn), .Q(j_k_ff_4_q[2]), .Qn(j_k_ff_2_qn), .reset(pc_reset));  // open: preset
  J_K_Flip_Flop j_k_ff_3 (
    .J(pc_en), .K(pc_en), .clk(j_k_ff_4_qn), .Q(j_k_ff_4_q[1]), .Qn(j_k_ff_3_qn), .reset(pc_reset));  // open: preset
  J_K_Flip_Flop j_k_ff_4 (
    .J(pc_en), .K(pc_en), .clk(pc_clk), .Q(j_k_ff_4_q[0]), .Qn(j_k_ff_4_qn), .reset(pc_reset));  // open: preset
  assign pc_out = pc_out_en ? j_k_ff_4_q : 4'bz;  // Controlled_Buffer controlled_buffer_1
endmodule

module fariaz_SRAM_cell (
  input  [7:0] data_in,
  input  write_en,
  input  clk,
  input  cs,
  input  read_en,
  output [7:0] memory_content,
  output [7:0] data_out
);

  wire and_1_out, and_2_out;

  and and_1 (and_1_out, write_en, cs);
  and and_2 (and_2_out, cs, read_en);
  fariaz_reg fariaz_reg_1 (
    .reg_in(data_in), .reg_in_en(and_1_out), .reg_clk(clk), .reg_out_en(and_2_out),
    .reg_int_out(memory_content), .reg_out(data_out));
endmodule

module fariaz_Ram (
  input  [7:0] sram_d_in,
  input  sram_rd,
  input  sram_wr,
  input  [7:0] mar_d_in,
  input  mar_in_en,
  input  sram_clk,
  output [7:0] sram_d_out,
  output [7:0] out_8,
  output [7:0] out_9,
  output [7:0] out_10,
  output [7:0] out_11,
  output [7:0] out_12,
  output [7:0] out_13,
  output [7:0] out_14,
  output [7:0] out_15,
  output [7:0] out_16,
  output [7:0] out_17,
  output [7:0] out_18,
  output [7:0] out_19,
  output [7:0] out_20,
  output [7:0] out_21,
  output [7:0] out_22,
  output [7:0] out_23
);

  wire decoder_1_out0, decoder_1_out1, decoder_1_out2, decoder_1_out4, decoder_1_out5, decoder_1_out6,
       decoder_1_out7, decoder_1_out8, decoder_1_out9, decoder_1_out10, decoder_1_out11, decoder_1_out12,
       decoder_1_out13, decoder_1_out14, decoder_1_out15;
  wire [7:0] fariaz_reg_1_reg_int_out, fariaz_sram_cell_1_data_out;

  fariaz_reg fariaz_reg_1 (
    .reg_in(mar_d_in), .reg_in_en(mar_in_en), .reg_clk(sram_clk), .reg_int_out(fariaz_reg_1_reg_int_out));  // open: reg_out_en, reg_out
  Decoder #(.select(4)) decoder_1 (
    .out0(decoder_1_out0), .out1(decoder_1_out1), .out2(decoder_1_out2), .out3(decoder_1_out2),
    .out4(decoder_1_out4), .out5(decoder_1_out5), .out6(decoder_1_out6), .out7(decoder_1_out7),
    .out8(decoder_1_out8), .out9(decoder_1_out9), .out10(decoder_1_out10), .out11(decoder_1_out11),
    .out12(decoder_1_out12), .out13(decoder_1_out13), .out14(decoder_1_out14), .out15(decoder_1_out15),
    .sel(fariaz_reg_1_reg_int_out[3:0]));  // open: en
  fariaz_SRAM_cell fariaz_sram_cell_1 (
    .data_in(fariaz_sram_cell_1_data_out), .write_en(sram_wr), .clk(sram_clk), .cs(decoder_1_out0),
    .read_en(sram_rd), .memory_content(out_8), .data_out(fariaz_sram_cell_1_data_out));
  fariaz_SRAM_cell fariaz_sram_cell_2 (
    .data_in(fariaz_sram_cell_1_data_out), .write_en(sram_wr), .cs(decoder_1_out1), .read_en(sram_rd),
    .memory_content(out_9), .data_out(fariaz_sram_cell_1_data_out));  // open: clk
  fariaz_SRAM_cell fariaz_sram_cell_3 (
    .data_in(fariaz_sram_cell_1_data_out), .write_en(sram_wr), .clk(sram_clk), .cs(decoder_1_out2),
    .read_en(sram_rd), .memory_content(out_10), .data_out(fariaz_sram_cell_1_data_out));
  fariaz_SRAM_cell fariaz_sram_cell_4 (
    .data_in(fariaz_sram_cell_1_data_out), .write_en(sram_wr), .clk(sram_clk), .cs(decoder_1_out2),
    .read_en(sram_rd), .memory_content(out_11), .data_out(fariaz_sram_cell_1_data_out));
  fariaz_SRAM_cell fariaz_sram_cell_5 (
    .data_in(fariaz_sram_cell_1_data_out), .write_en(sram_wr), .clk(sram_clk), .cs(decoder_1_out4),
    .read_en(sram_rd), .memory_content(out_12), .data_out(fariaz_sram_cell_1_data_out));
  fariaz_SRAM_cell fariaz_sram_cell_6 (
    .data_in(fariaz_sram_cell_1_data_out), .write_en(sram_wr), .clk(sram_clk), .cs(decoder_1_out5),
    .read_en(sram_rd), .memory_content(out_13), .data_out(fariaz_sram_cell_1_data_out));
  fariaz_SRAM_cell fariaz_sram_cell_7 (
    .data_in(fariaz_sram_cell_1_data_out), .write_en(sram_wr), .clk(sram_clk), .cs(decoder_1_out6),
    .read_en(sram_rd), .memory_content(out_14), .data_out(fariaz_sram_cell_1_data_out));
  fariaz_SRAM_cell fariaz_sram_cell_8 (
    .data_in(fariaz_sram_cell_1_data_out), .write_en(sram_wr), .clk(sram_clk), .cs(decoder_1_out7),
    .read_en(sram_rd), .memory_content(out_15), .data_out(fariaz_sram_cell_1_data_out));
  fariaz_SRAM_cell fariaz_sram_cell_9 (
    .data_in(fariaz_sram_cell_1_data_out), .write_en(sram_wr), .clk(sram_clk), .cs(decoder_1_out8),
    .read_en(sram_rd), .memory_content(out_16), .data_out(fariaz_sram_cell_1_data_out));
  fariaz_SRAM_cell fariaz_sram_cell_10 (
    .data_in(fariaz_sram_cell_1_data_out), .write_en(sram_wr), .clk(sram_clk), .cs(decoder_1_out9),
    .read_en(sram_rd), .memory_content(out_17), .data_out(fariaz_sram_cell_1_data_out));
  fariaz_SRAM_cell fariaz_sram_cell_11 (
    .data_in(fariaz_sram_cell_1_data_out), .write_en(sram_wr), .clk(sram_clk), .cs(decoder_1_out10),
    .read_en(sram_rd), .memory_content(out_18), .data_out(fariaz_sram_cell_1_data_out));
  fariaz_SRAM_cell fariaz_sram_cell_12 (
    .data_in(fariaz_sram_cell_1_data_out), .write_en(sram_wr), .clk(sram_clk), .cs(decoder_1_out11),
    .read_en(sram_rd), .memory_content(out_19), .data_out(fariaz_sram_cell_1_data_out));
  fariaz_SRAM_cell fariaz_sram_cell_13 (
    .data_in(fariaz_sram_cell_1_data_out), .write_en(sram_wr), .clk(sram_clk), .cs(decoder_1_out12),
    .read_en(sram_rd), .memory_content(out_20), .data_out(fariaz_sram_cell_1_data_out));
  fariaz_SRAM_cell fariaz_sram_cell_14 (
    .data_in(fariaz_sram_cell_1_data_out), .write_en(sram_wr), .clk(sram_clk), .cs(decoder_1_out13),
    .read_en(sram_rd), .memory_content(out_21), .data_out(fariaz_sram_cell_1_data_out));
  fariaz_SRAM_cell fariaz_sram_cell_15 (
    .data_in(fariaz_sram_cell_1_data_out), .write_en(sram_wr), .clk(sram_clk), .cs(decoder_1_out14),
    .read_en(sram_rd), .memory_content(out_22), .data_out(fariaz_sram_cell_1_data_out));
  fariaz_SRAM_cell fariaz_sram_cell_16 (
    .data_in(fariaz_sram_cell_1_data_out), .write_en(sram_wr), .clk(sram_clk), .cs(decoder_1_out15),
    .read_en(sram_rd), .memory_content(out_23), .data_out(fariaz_sram_cell_1_data_out));
  assign fariaz_sram_cell_1_data_out = sram_wr ? sram_d_in : 8'bz;  // Controlled_Buffer controlled_buffer_1
  assign sram_d_out = sram_rd ? fariaz_sram_cell_1_data_out : 8'bz;  // Controlled_Buffer controlled_buffer_2
endmodule

module fariaz_IR (
  input  [7:0] ins_reg_in,
  input  ins_reg_in_en,
  input  clk,
  input  ins_reg_out_en,
  output [3:0] add_outs,
  output [3:0] ins_out
);

  wire [3:0] fariaz_reg_1_reg_int_out;
  wire [7:0] fariaz_reg_1_reg_out;

  fariaz_reg fariaz_reg_1 (
    .reg_in(ins_reg_in), .reg_in_en(ins_reg_in_en), .reg_clk(clk),
    .reg_int_out({ins_out, fariaz_reg_1_reg_int_out}), .reg_out(fariaz_reg_1_reg_out));  // open: reg_out_en
  assign add_outs = ins_reg_out_en ? fariaz_reg_1_reg_int_out : 4'bz;  // Controlled_Buffer controlled_buffer_1
endmodule

module fariaz_Final (
  input  in_1,
  input  CLK,
  input  OPERATION_MODE,
  input  UPLOAD_MODE,
  input  in_5,
  input  RESET,
  input  in_7,
  input  in_8,
  input  [7:0] in_9,
  output [7:0] out_10,
  output [7:0] out_11,
  output [7:0] out_12,
  output [3:0] out_13,
  output [7:0] out_14,
  output [7:0] out_15,
  output [7:0] out_16,
  output [7:0] out_17,
  output [7:0] out_18,
  output [7:0] out_19,
  output [7:0] out_20,
  output out_21,
  output [7:0] out_22,
  output out_23,
  output [7:0] out_24,
  output out_25,
  output [7:0] out_26,
  output out_27,
  output [7:0] out_28,
  output out_29,
  output [7:0] out_30,
  output out_31,
  output [7:0] out_32,
  output HLT,
  output [7:0] out_34,
  output [7:0] out_35,
  output [7:0] out_36
);

  wire A_IN, A_OUT, ALU_OUT, ALU_SUB, B_IN, B_OUT, control_sequencer_1_mar_in_en, control_sequencer_1_pc_out,
       controlled_buffer_4_out, INS_REG_IN_EN, INS_REG_OUT_EN, MAR_IN_EN, PC_EN, PC_OUT_EN, SRAM_RD;
  wire [3:0] fariaz_ir_1_ins_out;
  wire [7:0] fariaz_reg_2_reg_int_out;

  fariaz_pc fariaz_pc_1 (.pc_en(PC_EN), .pc_clk(CLK), .pc_reset(in_1), .pc_out_en(PC_OUT_EN), .pc_out(out_13));
  fariaz_Ram fariaz_ram_1 (
    .sram_d_in({out_36[7:4], out_13}), .sram_rd(SRAM_RD), .sram_wr(in_7), .mar_d_in({out_36[7:4], out_13}),
    .mar_in_en(MAR_IN_EN), .sram_clk(CLK), .sram_d_out({out_36[7:4], out_13}), .out_8(out_11),
    .out_9(out_12), .out_10(out_14), .out_11(out_16), .out_12(out_17), .out_13(out_18), .out_14(out_19),
    .out_15(out_20), .out_16(out_22), .out_17(out_24), .out_18(out_26), .out_19(out_28), .out_20(out_30),
    .out_21(out_32), .out_22(out_34), .out_23(out_35));
  assign {out_36[7:4], out_13} = in_8 ? in_9 : 8'bz;  // Controlled_Buffer controlled_buffer_1
  fariaz_reg fariaz_reg_1 (
    .reg_in({out_36[7:4], out_13}), .reg_in_en(A_IN), .reg_clk(CLK), .reg_out_en(A_OUT),
    .reg_int_out(out_10), .reg_out({out_36[7:4], out_13}));
  fariaz_reg fariaz_reg_2 (
    .reg_in({out_36[7:4], out_13}), .reg_in_en(B_IN), .reg_clk(CLK), .reg_out_en(B_OUT),
    .reg_int_out(fariaz_reg_2_reg_int_out), .reg_out({out_36[7:4], out_13}));
  fariaz_IR fariaz_ir_1 (
    .ins_reg_in({out_36[7:4], out_13}), .ins_reg_in_en(INS_REG_IN_EN), .clk(CLK),
    .ins_reg_out_en(INS_REG_OUT_EN), .add_outs(out_13), .ins_out(fariaz_ir_1_ins_out));
  control_sequencer control_sequencer_1 (
    .I7(fariaz_ir_1_ins_out[3]), .I6(fariaz_ir_1_ins_out[2]), .I5(fariaz_ir_1_ins_out[1]),
    .I4(fariaz_ir_1_ins_out[0]), .CLK(controlled_buffer_4_out), .RESET(RESET), .T1(out_21), .T2(out_23),
    .T3(out_25), .T4(out_27), .T5(out_29), .T6(out_31), .HLT(HLT), .ALU_OUT(ALU_OUT), .A_OUT(A_OUT),
    .ALU_sub(ALU_SUB), .PC_EN(PC_EN), .MAR_IN_EN(control_sequencer_1_mar_in_en), .SRAM_RD(SRAM_RD),
    .INS_REG_OUT_EN(INS_REG_OUT_EN), .A_IN(A_IN), .B_IN(B_IN), .PC_OUT(control_sequencer_1_pc_out),
    .INS_REG_IN_EN(INS_REG_IN_EN));
  fariaz_alu fariaz_alu_1 (
    .alu_in_1(out_10), .alu_out_in(ALU_OUT), .alu_sub(ALU_SUB), .alu_in_2(fariaz_reg_2_reg_int_out),
    .alu_out({out_36[7:4], out_13}));  // open: alu_carry_out
  assign PC_OUT_EN = OPERATION_MODE ? control_sequencer_1_pc_out : 1'bz;  // Controlled_Buffer controlled_buffer_2
  assign MAR_IN_EN = OPERATION_MODE ? control_sequencer_1_mar_in_en : 1'bz;  // Controlled_Buffer controlled_buffer_3
  assign controlled_buffer_4_out = OPERATION_MODE ? CLK : 1'bz;  // Controlled_Buffer controlled_buffer_4
  assign MAR_IN_EN = UPLOAD_MODE ? in_5 : 1'bz;  // Controlled_Buffer controlled_buffer_5

  assign out_36[3:0] = out_13;

  // Other names for the same wires on the sheet: DEBUG = in_8; DEBUG_DATA[7:0] = in_9; PC_RESET = in_1;
  //   SRAM_WR = in_7
endmodule

module control_sequencer (
  input  I7,
  input  I6,
  input  I5,
  input  I4,
  input  CLK,
  input  RESET,
  output T1,
  output T2,
  output T3,
  output T4,
  output T5,
  output T6,
  output HLT,
  output ALU_OUT,
  output A_OUT,
  output ALU_sub,
  output PC_EN,
  output MAR_IN_EN,
  output SRAM_RD,
  output INS_REG_OUT_EN,
  output A_IN,
  output B_IN,
  output PC_OUT,
  output INS_REG_IN_EN
);

  wire and_1_out, and_2_out, and_3_out, and_4_out, and_6_out, and_7_out, and_8_out, and_9_out, and_10_out,
       and_11_out, and_12_out, and_13_out, and_14_out, and_15_out, and_16_out, j_k_ff_1_q, j_k_ff_2_qn,
       j_k_ff_3_qn, j_k_ff_4_qn, j_k_ff_5_qn, j_k_ff_6_qn, not_1_out, not_2_out, not_3_out, not_4_out,
       or_1_out, or_4_out, or_7_out, or_8_out, or_9_out;

  not not_1 (not_1_out, I7);
  not not_2 (not_2_out, I5);
  not not_3 (not_3_out, I6);
  not not_4 (not_4_out, I4);
  and and_1 (and_1_out, I4, I5, not_3_out, not_1_out);
  and and_2 (and_2_out, I4, not_2_out, not_3_out, not_1_out);
  and and_3 (and_3_out, not_4_out, I5, not_3_out, not_1_out);
  and and_4 (and_4_out, not_4_out, I5, I6, I7);
  and and_5 (HLT, I4, I5, I6, I7);
  J_K_Flip_Flop j_k_ff_1 (
    .J(j_k_ff_6_qn), .K(T6), .clk(CLK), .Q(j_k_ff_1_q), .Qn(PC_OUT), .reset(RESET));  // open: preset
  J_K_Flip_Flop j_k_ff_2 (
    .J(PC_OUT), .K(j_k_ff_1_q), .clk(CLK), .Q(INS_REG_IN_EN), .Qn(j_k_ff_2_qn), .reset(RESET));  // open: preset
  or or_1 (or_1_out, and_1_out, and_3_out);
  and and_6 (and_6_out, T4, and_2_out);
  and and_7 (and_7_out, T4, or_1_out);
  or or_2 (MAR_IN_EN, PC_OUT, and_6_out, and_7_out, and_8_out);
  J_K_Flip_Flop j_k_ff_3 (
    .J(INS_REG_IN_EN), .K(j_k_ff_2_qn), .clk(CLK), .Q(PC_EN), .Qn(j_k_ff_3_qn), .reset(RESET));  // open: preset
  and and_8 (and_8_out, T4, and_4_out);
  and and_9 (and_9_out, T5, and_2_out);
  and and_10 (and_10_out, T5, or_4_out);
  or or_3 (SRAM_RD, INS_REG_IN_EN, and_9_out, and_10_out, and_11_out);
  J_K_Flip_Flop j_k_ff_4 (
    .J(PC_EN), .K(j_k_ff_3_qn), .clk(CLK), .Q(T4), .Qn(j_k_ff_4_qn), .reset(RESET));  // open: preset
  or or_4 (or_4_out, and_1_out, and_3_out);
  and and_11 (and_11_out, T5, and_4_out);
  J_K_Flip_Flop j_k_ff_5 (.J(T4), .K(j_k_ff_4_qn), .clk(CLK), .Q(T5), .Qn(j_k_ff_5_qn), .reset(RESET));  // open: preset
  and and_12 (and_12_out, T4, and_1_out);
  and and_13 (and_13_out, T4, and_2_out);
  and and_14 (and_14_out, T4, and_3_out);
  or or_5 (INS_REG_OUT_EN, and_12_out, and_13_out, and_14_out);
  J_K_Flip_Flop j_k_ff_6 (.J(T5), .K(j_k_ff_5_qn), .clk(CLK), .Q(T6), .Qn(j_k_ff_6_qn), .reset(RESET));  // open: preset
  and and_15 (and_15_out, T5, and_2_out);
  or or_6 (A_IN, and_15_out, and_16_out);
  or or_7 (or_7_out, and_3_out, and_1_out);
  and and_16 (and_16_out, T6, or_7_out);
  or or_8 (or_8_out, and_1_out, and_3_out);
  and and_17 (B_IN, T5, or_8_out);
  or or_9 (or_9_out, and_1_out, and_3_out);
  and and_18 (ALU_OUT, T6, or_9_out);
  and and_19 (A_OUT, T4, and_4_out);
  and and_20 (ALU_sub, T6, and_1_out);

  assign T1 = PC_OUT;
  assign T2 = INS_REG_IN_EN;
  assign T3 = PC_EN;

  // Notes on the sheet:
  //   SUB
  //   LDA
  //   ADD
  //   OUT
endmodule
